# Fritzing sketch otopark_proje (saved by Fritzing 0.9.4)

parts:
  U2 = ESP32S-HiLetgo [part_number=ESP32S-HiLetgo]
  HC-SR04_Sensor_1 = HC-SR04 Ultrasonic Distance Sensor
  HC-SR04_Sensor_2 = HC-SR04 Ultrasonic Distance Sensor
  J1 = Basic Servo

nets:
  N1: U2.GPIO35, HC-SR04_Sensor_2.TRIG
  N2: U2.GPIO32, HC-SR04_Sensor_2.ECHO
  N3: U2.GPIO9, J1.pulse
  GND: U2.GPIO11, HC-SR04_Sensor_2.GND, J1.gnd
  VCC: U2.VIN, HC-SR04_Sensor_2.VCC, J1.vcc
  N4: U2.GPIO6, HC-SR04_Sensor_1.VCC
  N5: U2.GPIO7, HC-SR04_Sensor_1.GND
  N6: U2.GPIO15, HC-SR04_Sensor_1.ECHO
  N7: U2.GPIO2, HC-SR04_Sensor_1.TRIG

custom parts:
  ESP32S-HiLetgo: HiLetgo ESP-WROOM-32 ESP32 ESP-32S Development Board 2.4GHz Dual-Mode WiFi + Bluetooth Dual Cores Microcontroller The ESP32 integrated with Antenna switches, RF Balun, power amplifiers, low-noise amplifiers, filters, and management modules, and the entire solution occupies the least area of PCB. 2.4 GHz Wi-Fi plus Bluetooth dual-mode chip, with TSMC Ultra-low power consumption 40nm technology,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
  Basic Servo: A generic servo.
